// Logisim project ACCUMULATOR.circ as structural Verilog: 1 circuit, main circuit main
module main (
  input  A3,
  input  A2,
  input  A1,
  input  A0,
  input  in_5,
  output F3,
  output F2,
  output F1,
  output F0
);

  wire clock_1_out, multiplexer_1_out, multiplexer_2_out, multiplexer_3_out, multiplexer_4_out;

  D_Flip_Flop d_ff_1 (.D(multiplexer_1_out), .clk(clock_1_out), .Q(F3));  // open: Qn, preset, reset
  Multiplexer multiplexer_1 (.in0(F3), .in1(A3), .out(multiplexer_1_out), .sel(in_5));
  Clock clock_1 (.out(clock_1_out));
  D_Flip_Flop d_ff_2 (.D(multiplexer_2_out), .clk(clock_1_out), .Q(F2));  // open: Qn, preset, reset
  Multiplexer multiplexer_2 (.in0(F2), .in1(A2), .out(multiplexer_2_out), .sel(in_5));
  Multiplexer multiplexer_3 (.in0(F1), .in1(A1), .out(multiplexer_3_out), .sel(in_5));
  D_Flip_Flop d_ff_3 (.D(multiplexer_3_out), .clk(clock_1_out), .Q(F1));  // open: Qn, preset, reset
  D_Flip_Flop d_ff_4 (.D(multiplexer_4_out), .clk(clock_1_out), .Q(F0));  // open: Qn, preset, reset
  Multiplexer multiplexer_4 (.in0(F0), .in1(A0), .out(multiplexer_4_out), .sel(in_5));

  // Notes on the sheet:
  //   ALU RESULT
  //   ALU_INPUT
endmodule
