// Logisim project accumulator_v2.circ as structural Verilog: 1 circuit, main circuit main
module main (
  input  [3:0] \input ,
  input  ACC_LOAD,
  output [3:0] \output 
);

  wire CLK_out, multiplexer_1_out, multiplexer_2_out, multiplexer_3_out, multiplexer_4_out;

  Clock CLK (.out(CLK_out));
  D_Flip_Flop d_ff_1 (.D(multiplexer_1_out), .clk(CLK_out), .Q(\output [3]));  // open: Qn, preset, reset
  Multiplexer multiplexer_1 (.in0(\output [3]), .in1(\input [3]), .out(multiplexer_1_out), .sel(ACC_LOAD));
  Multiplexer multiplexer_2 (.in0(\output [2]), .in1(\input [2]), .out(multiplexer_2_out), .sel(ACC_LOAD));
  D_Flip_Flop d_ff_2 (.D(multiplexer_2_out), .clk(CLK_out), .Q(\output [2]));  // open: Qn, preset, reset
  D_Flip_Flop d_ff_3 (.D(multiplexer_3_out), .clk(CLK_out), .Q(\output [1]));  // open: Qn, preset, reset
  Multiplexer multiplexer_3 (.in0(\output [1]), .in1(\input [1]), .out(multiplexer_3_out), .sel(ACC_LOAD));
  D_Flip_Flop d_ff_4 (.D(multiplexer_4_out), .clk(CLK_out), .Q(\output [0]));  // open: Qn, preset, reset
  Multiplexer multiplexer_4 (.in0(\output [0]), .in1(\input [0]), .out(multiplexer_4_out), .sel(ACC_LOAD));
endmodule
